# Fritzing sketch robosub_v1 (saved by Fritzing 1.0.6)

parts:
  Part1 = Arduino Uno (Rev3) - ICSP
  Adafruit_Feather_ESP32-C1 = Adafruit Feather ESP32-C6 [mn=Adafruit mpn=#5933 part_number=#5933]
  Part2 = Adafruit PCA9685 PWM/Servo Breakout [part_number=815]
  A1 = Raspberry Pi 5
  A4 = Littlebee 40A ESC
  A8 = Littlebee 40A ESC
  A9 = Littlebee 40A ESC
  A10 = Littlebee 40A ESC
  U1 = LIPO-110mAh [package=lipo-110]
  J1 = Basic Servo
  J2 = Basic Servo
  Part3 = Adafruit BNO085 9-DOF Orientation IMU Fusion [part_number="Addfruit #4754"]
  A11 = Littlebee 40A ESC
  A12 = Littlebee 40A ESC

nets:
  VCC: Part1.5V, J1.vcc, J2.vcc
  N1: Part1.D3_PWM, J1.pulse
  N2: Part1.D5_PWM, J2.pulse
  GND: Part1.GND, J1.gnd, J2.gnd
  GND_2: Adafruit_Feather_ESP32-C1.GND, Part2.GND, A4.Pin_6, A8.Pin_6, A9.Pin_6, A10.Pin_6, U1.-, A11.Pin_6, A12.Pin_6
  3.3V: Adafruit_Feather_ESP32-C1.3.3V, Part2.VCC
  N3: Adafruit_Feather_ESP32-C1.VBAT, U1.+
  N4: Adafruit_Feather_ESP32-C1.SCL, Part2.SCL
  N5: Adafruit_Feather_ESP32-C1.SDA, Part2.SDA
  N6: Part2.PWM5, A12.Pin_8
  N7: Part2.5.0V, A4.Pin_7, A8.Pin_7, A9.Pin_7, A10.Pin_7, A11.Pin_7, A12.Pin_7
  N8: Part2.PWM4, A11.Pin_8
  N9: Part2.PWM3, A9.Pin_8
  N10: Part2.PWM2, A10.Pin_8
  N11: Part2.PWM1, A8.Pin_8
  N12: Part2.PWM0, A4.Pin_8
  3V3: A1.3V3, Part3.VCC
  N13: A1.GPIO2, Part3.SDA/MISO/TX
  N14: A1.GPIO3, Part3.SCL/SCK/RX
  GND_3: A1.GND, Part3.GND

custom parts:
  Adafruit PCA9685 PWM/Servo Breakout: Using only two pins, control 16 free-running PWM outputs! I2C-controlled PWM driver with a built in clock. Unlike the TLC5940 family, you do not need to continuously send it signal tying up your microcontroller, its completely free running! 5V compliant, which means you can control it from a 3.3V microcontroller and still safely drive up to 6V outputs (this is good for when you want to control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
  Raspberry Pi 5: The RPi5, a faster version of the awesome Raspberry Pi4B ARM Board with 40 pin gpio.
  Littlebee 40A ESC: LittleBee 40A 2-4 LiPo Battery ESC Brushless Speed Controller for RC FPV Multicopter.
